# Fritzing sketch PTZ1 (saved by Fritzing 0.9.4)
circuit board: 5.9cm x 5cm
breadboards: 2

parts:
  Arduino_Nano = Arduino Nano (Rev3.0)
  WIZ850io = WIZ850io [part_number=WIZ850io]
  RXTX = female pin header, 5 pins [form="♀ (female)"]
  MT = male pin header, 4 pins [form="♂ (male)"]
  J1 = female pin header, 6 pins [form="♀ (female)"]
  J2 = male pin header, 8 pins [form="♂ (male)"]
  C2 = Electrolytic Capacitor [capacitance=0.33nF package="100 mil [THT, electrolytic]"]
  U1 = Voltage Regulator - 5V [package="TO220 [THT]"]
  TB6612FNG = SparkFun Motor Driver TB6612FNG (v11) [part_number=ROB-14451]
  V+ = male pin header, 3 pins [form="♂ (male)"]
  Q1 = MCP1700 [package=to-92]
  C4 = Ceramic Capacitor [capacitance=1µF package="100 mil [THT, multilayer]"]
  C3 = Ceramic Capacitor [capacitance=1µF package="100 mil [THT, multilayer]"]
  C1 = Electrolytic Capacitor [capacitance=0.1nF package="100 mil [THT, electrolytic]"]

nets:
  N1: Arduino_Nano.D1/TX, RXTX.pin1
  N2: Arduino_Nano.D0/RX, RXTX.pin2
  N3: Arduino_Nano.RESET, RXTX.pin3, J1.pin3
  N4: Arduino_Nano.GND, RXTX.pin4, RXTX.pin5, J1.pin2
  N5: Arduino_Nano.D2, TB6612FNG.STBY
  N6: Arduino_Nano.D3, TB6612FNG.PWMA
  N7: Arduino_Nano.D4, TB6612FNG.AIN2
  N8: Arduino_Nano.D5, TB6612FNG.AIN1
  N9: Arduino_Nano.D6, TB6612FNG.PWMB
  N10: Arduino_Nano.D7, TB6612FNG.BIN1
  N11: Arduino_Nano.D8, TB6612FNG.BIN2
  N12: Arduino_Nano.D9, WIZ850io.nRESET
  N13: Arduino_Nano.D10, WIZ850io.nSCN
  N14: Arduino_Nano.D11/MOSI, WIZ850io.MOSI
  N15: Arduino_Nano.D12/MISO, WIZ850io.MISO
  N16: Arduino_Nano.VIN, J1.pin1, C2.+, U1.input_voltage, V+.pin1
  5V: Arduino_Nano.5V, J1.pin4, TB6612FNG.VCC, Q1.VIN, C4.0
  N17: Arduino_Nano.A7, J1.pin5
  N18: Arduino_Nano.A6, J1.pin6
  N19: Arduino_Nano.A5, J2.pin1
  N20: Arduino_Nano.A4, J2.pin2
  N21: Arduino_Nano.A3, J2.pin3
  N22: Arduino_Nano.A2, J2.pin4
  N23: Arduino_Nano.A1, J2.pin5
  N24: Arduino_Nano.A0, J2.pin6
  N25: Arduino_Nano.AREF, J2.pin7
  N26: Arduino_Nano.3V3, J2.pin8
  N27: Arduino_Nano.D13/SCK, WIZ850io.SCLK
  GND: WIZ850io.GND, TB6612FNG.GND, V+.pin2, V+.pin3
  N28: WIZ850io.VIN, Q1.VOUT, C3.0
  N29: MT.pin1, TB6612FNG.A01
  N30: MT.pin2, TB6612FNG.A02
  N31: MT.pin3, TB6612FNG.B02
  N32: MT.pin4, TB6612FNG.B01
  N33: C2.-, U1.GND, C1.-
  N34: U1.output_voltage, TB6612FNG.VM, C1.+
  N35: Q1.GND, C4.1, C3.1

notes:
  PTZ V1.1
  TGV
  B
  A
  3.3V

custom parts:
  WIZ850io: Plug-in Network Module having W5500 & Mag Jack
  SparkFun Motor Driver TB6612FNG (v11): The TB6612FNG Motor Driver can control up to two DC motors at a constant current of 1.2A (3.2A peak). Two input signals (IN1 and IN2) can be used to control the motor in one of four function modes: CW, CCW, short-brake and stop. The two motor outputs (A and B) can be separately controlled, and the speed of each motor is controlled via a PWM input signal with a frequency up to 100kHz. The STBY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
