# Fritzing sketch lanc (saved by Fritzing 0.9.4)
circuit board: 2.6cm x 1.8cm
breadboards: 1

parts:
  R2 = Resistor [tolerance=±5% resistance=4.7k package=THT]
  R1 = Resistor [tolerance=±5% resistance=5.6k package=THT]
  Q1 = NPN-Transistor [package="TO92 [THT]"]
  D1 = Zener Diode [part_number=1N4732A breakdown_voltage=5.1V package="300 mil [THT]"]
  J4 = male pin header, 2 pins [form="♂ (male)"]
  J5 = male pin header, 3 pins [form="♂ (male)"]
  J2 = male pin header, 5 pins [form="♂ (male)"]
  J3 = male pin header, 6 pins [form="♂ (male)"]

nets:
  N1: R2.Pin_0, Q1.C, D1.cathode, J5.pin2, J3.pin6
  N2: R2.Pin_1, J4.pin1, J5.pin1
  N3: R1.Pin_0, Q1.B
  N4: R1.Pin_1, J3.pin5
  GND: Q1.E, D1.anode, J5.pin3, J2.pin4, J3.pin2
  N5: J4.pin2, J3.pin1

notes:
  V+
  GND
  LANC
